// Logisim project 32bit_riscv_cpu.circ as structural Verilog: 3 circuits, main circuit main
module main (
);

  wire clock_1_out;
  wire [4:0] rom_1_data, rom_1_data_3;
  wire [6:0] rom_1_data_4;
  wire [19:0] rom_1_data_2;
  wire [23:0] counter_1_q;
  wire [31:0] alu_1_alu_out, register_file_1_rs1_out, register_file_1_rs2_out;

  Clock clock_1 (.out(clock_1_out));
  ROM #(.addrWidth(24), .dataWidth(32)) rom_1 (
    .addr(counter_1_q),
    .data({rom_1_data_2[19:13], rom_1_data, rom_1_data_2[7:0], rom_1_data_3, rom_1_data_4}));
  Counter #(.max('hffffff), .width(24)) counter_1 (
    .Q(counter_1_q), .clk(clock_1_out));  // open: load, D, count, carry, up, clr
  register_file register_file_1 (
    .rd_in(rom_1_data_3), .CLK(clock_1_out), .data_in(alu_1_alu_out), .rs1_in(rom_1_data_2[7:3]),
    .rs2_in(rom_1_data), .rs1_out(register_file_1_rs1_out), .rs2_out(register_file_1_rs2_out));  // open: RESET
  alu alu_1 (
    .rs2_out(register_file_1_rs2_out), .rs1_out(register_file_1_rs1_out), .funct7(rom_1_data_2[19:13]),
    .funct3(rom_1_data_2[2:0]), .alu_out(alu_1_alu_out));

  // Notes on the sheet:
  //   contents of rom_1 (hex, n*v repeats v):
  //   40208233
  //   f7
  //   imm[11:5]
  //   rs2
  //   rs2
  //   imm[31:12]
  //   R-Type
  //   rs1
  //   f3
  //   S-Type
  //   rs1
  //   f3
  //   U-Type
  //   rd
  //   op
  //   imm[4:0]
  //   rd
  //   op
  //   op
  //   imm[11:0]
  //   imm[12|10:5]
  //   rs1
  //   rs1
  //   rs2
  //   imm[20|10:1|11|19:12]
  //   I-Type
  //   f3
  //   rd
  //   B-Type
  //   f3
  //   J-Type
  //   op
  //   op
  //   imm[4:1|11]
  //   rd
  //   op
endmodule

module register_file (
  input  [4:0] rd_in,
  input  CLK,
  input  RESET,
  input  [31:0] data_in,
  input  [4:0] rs1_in,
  input  [4:0] rs2_in,
  output [31:0] rs1_out,
  output [31:0] rs2_out
);

  wire [2:0] demultiplexer_1_out1;
  wire [3:0] demultiplexer_1_out4, demultiplexer_1_out8, demultiplexer_1_out12, demultiplexer_1_out16,
       demultiplexer_1_out20, demultiplexer_1_out24, demultiplexer_1_out28;
  wire [31:0] register_1_q, register_2_q, register_3_q, register_4_q, register_5_q, register_6_q,
       register_7_q, register_8_q, register_9_q, register_10_q, register_11_q, register_12_q, register_13_q,
       register_14_q, register_15_q, register_16_q, register_17_q, register_18_q, register_19_q,
       register_20_q, register_21_q, register_22_q, register_23_q, register_24_q, register_25_q,
       register_26_q, register_27_q, register_28_q, register_29_q, register_30_q, register_31_q;

  Register #(.width(32)) register_1 (
    .D(data_in), .en(demultiplexer_1_out1[0]), .clk(CLK), .Q(register_1_q), .clr(RESET));
  Register #(.width(32)) register_2 (
    .D(data_in), .en(demultiplexer_1_out1[1]), .clk(CLK), .Q(register_2_q), .clr(RESET));
  Register #(.width(32)) register_3 (
    .D(data_in), .en(demultiplexer_1_out1[2]), .clk(CLK), .Q(register_3_q), .clr(RESET));
  Register #(.width(32)) register_4 (
    .D(data_in), .en(demultiplexer_1_out16[0]), .clk(CLK), .Q(register_4_q), .clr(RESET));
  Register #(.width(32)) register_5 (
    .D(data_in), .en(demultiplexer_1_out16[1]), .clk(CLK), .Q(register_5_q), .clr(RESET));
  Register #(.width(32)) register_6 (
    .D(data_in), .en(demultiplexer_1_out16[2]), .clk(CLK), .Q(register_6_q), .clr(RESET));
  Register #(.width(32)) register_7 (
    .D(data_in), .en(demultiplexer_1_out16[3]), .clk(CLK), .Q(register_7_q), .clr(RESET));
  Demultiplexer #(.select(5)) demultiplexer_1 (
    .out1(demultiplexer_1_out1[0]), .out2(demultiplexer_1_out1[1]), .out3(demultiplexer_1_out1[2]),
    .out4(demultiplexer_1_out4[0]), .out5(demultiplexer_1_out4[1]), .out6(demultiplexer_1_out4[2]),
    .out7(demultiplexer_1_out4[3]), .out8(demultiplexer_1_out8[0]), .out9(demultiplexer_1_out8[1]),
    .out10(demultiplexer_1_out8[2]), .out11(demultiplexer_1_out8[3]), .out12(demultiplexer_1_out12[0]),
    .out13(demultiplexer_1_out12[1]), .out14(demultiplexer_1_out12[2]), .out15(demultiplexer_1_out12[3]),
    .out16(demultiplexer_1_out16[0]), .out17(demultiplexer_1_out16[1]), .out18(demultiplexer_1_out16[2]),
    .out19(demultiplexer_1_out16[3]), .out20(demultiplexer_1_out20[0]), .out21(demultiplexer_1_out20[1]),
    .out22(demultiplexer_1_out20[2]), .out23(demultiplexer_1_out20[3]), .out24(demultiplexer_1_out24[0]),
    .out25(demultiplexer_1_out24[1]), .out26(demultiplexer_1_out24[2]), .out27(demultiplexer_1_out24[3]),
    .out28(demultiplexer_1_out28[0]), .out29(demultiplexer_1_out28[1]), .out30(demultiplexer_1_out28[2]),
    .out31(demultiplexer_1_out28[3]), .sel(rd_in));  // open: out0, in
  Register #(.width(32)) register_8 (
    .D(data_in), .en(demultiplexer_1_out4[0]), .clk(CLK), .Q(register_8_q), .clr(RESET));
  Register #(.width(32)) register_9 (
    .D(data_in), .en(demultiplexer_1_out4[1]), .clk(CLK), .Q(register_9_q), .clr(RESET));
  Register #(.width(32)) register_10 (
    .D(data_in), .en(demultiplexer_1_out4[2]), .clk(CLK), .Q(register_10_q), .clr(RESET));
  Register #(.width(32)) register_11 (
    .D(data_in), .en(demultiplexer_1_out4[3]), .clk(CLK), .Q(register_11_q), .clr(RESET));
  Register #(.width(32)) register_12 (
    .D(data_in), .en(demultiplexer_1_out20[0]), .clk(CLK), .Q(register_12_q), .clr(RESET));
  Register #(.width(32)) register_13 (
    .D(data_in), .en(demultiplexer_1_out20[1]), .clk(CLK), .Q(register_13_q), .clr(RESET));
  Register #(.width(32)) register_14 (
    .D(data_in), .en(demultiplexer_1_out20[2]), .clk(CLK), .Q(register_14_q), .clr(RESET));
  Register #(.width(32)) register_15 (
    .D(data_in), .en(demultiplexer_1_out20[3]), .clk(CLK), .Q(register_15_q), .clr(RESET));
  Register #(.width(32)) register_16 (
    .D(data_in), .en(demultiplexer_1_out8[0]), .clk(CLK), .Q(register_16_q), .clr(RESET));
  Register #(.width(32)) register_17 (
    .D(data_in), .en(demultiplexer_1_out8[1]), .clk(CLK), .Q(register_17_q), .clr(RESET));
  Register #(.width(32)) register_18 (
    .D(data_in), .en(demultiplexer_1_out8[2]), .clk(CLK), .Q(register_18_q), .clr(RESET));
  Register #(.width(32)) register_19 (
    .D(data_in), .en(demultiplexer_1_out8[3]), .clk(CLK), .Q(register_19_q), .clr(RESET));
  Register #(.width(32)) register_20 (
    .D(data_in), .en(demultiplexer_1_out24[0]), .clk(CLK), .Q(register_20_q), .clr(RESET));
  Register #(.width(32)) register_21 (
    .D(data_in), .en(demultiplexer_1_out24[1]), .clk(CLK), .Q(register_21_q), .clr(RESET));
  Register #(.width(32)) register_22 (
    .D(data_in), .en(demultiplexer_1_out24[2]), .clk(CLK), .Q(register_22_q), .clr(RESET));
  Register #(.width(32)) register_23 (
    .D(data_in), .en(demultiplexer_1_out24[3]), .clk(CLK), .Q(register_23_q), .clr(RESET));
  Multiplexer #(.select(5), .width(32)) multiplexer_1 (
    .in0({32{1'b0}}), .in1(register_1_q), .in2(register_2_q), .in3(register_3_q), .in4(register_8_q),
    .in5(register_9_q), .in6(register_10_q), .in7(register_11_q), .in8(register_16_q), .in9(register_17_q),
    .in10(register_18_q), .in11(register_19_q), .in12(register_24_q), .in13(register_25_q),
    .in14(register_26_q), .in15(register_27_q), .in16(register_4_q), .in17(register_5_q),
    .in18(register_6_q), .in19(register_7_q), .in20(register_12_q), .in21(register_13_q),
    .in22(register_14_q), .in23(register_15_q), .in24(register_20_q), .in25(register_21_q),
    .in26(register_22_q), .in27(register_23_q), .in28(register_28_q), .in29(register_29_q),
    .in30(register_30_q), .in31(register_31_q), .out(rs2_out), .sel(rs2_in));
  Register #(.width(32)) register_24 (
    .D(data_in), .en(demultiplexer_1_out12[0]), .clk(CLK), .Q(register_24_q), .clr(RESET));
  Register #(.width(32)) register_25 (
    .D(data_in), .en(demultiplexer_1_out12[1]), .clk(CLK), .Q(register_25_q), .clr(RESET));
  Register #(.width(32)) register_26 (
    .D(data_in), .en(demultiplexer_1_out12[2]), .clk(CLK), .Q(register_26_q), .clr(RESET));
  Register #(.width(32)) register_27 (
    .D(data_in), .en(demultiplexer_1_out12[3]), .clk(CLK), .Q(register_27_q), .clr(RESET));
  Register #(.width(32)) register_28 (
    .D(data_in), .en(demultiplexer_1_out28[0]), .clk(CLK), .Q(register_28_q), .clr(RESET));
  Register #(.width(32)) register_29 (
    .D(data_in), .en(demultiplexer_1_out28[1]), .clk(CLK), .Q(register_29_q), .clr(RESET));
  Register #(.width(32)) register_30 (
    .D(data_in), .en(demultiplexer_1_out28[2]), .clk(CLK), .Q(register_30_q), .clr(RESET));
  Register #(.width(32)) register_31 (
    .D(data_in), .en(demultiplexer_1_out28[3]), .clk(CLK), .Q(register_31_q), .clr(RESET));
  Multiplexer #(.select(5), .width(32)) multiplexer_2 (
    .in0({32{1'b0}}), .in1(register_1_q), .in2(register_2_q), .in3(register_3_q), .in4(register_8_q),
    .in5(register_9_q), .in6(register_10_q), .in7(register_11_q), .in8(register_16_q), .in9(register_17_q),
    .in10(register_18_q), .in11(register_19_q), .in12(register_24_q), .in13(register_25_q),
    .in14(register_26_q), .in15(register_27_q), .in16(register_4_q), .in17(register_5_q),
    .in18(register_6_q), .in19(register_7_q), .in20(register_12_q), .in21(register_13_q),
    .in22(register_14_q), .in23(register_15_q), .in24(register_20_q), .in25(register_21_q),
    .in26(register_22_q), .in27(register_23_q), .in28(register_28_q), .in29(register_29_q),
    .in30(register_30_q), .in31(register_31_q), .out(rs1_out), .sel(rs1_in));
endmodule

module alu (
  input  [31:0] rs2_out,
  input  [31:0] rs1_out,
  input  [6:0] funct7,
  input  [2:0] funct3,
  output [31:0] alu_out
);

  wire comparator_1_lt, comparator_2_lt, comparator_3_eq;
  wire [7:0] rom_1_data;
  wire [31:0] adder_1_out, and_1_out, bit_extender_1_out, bit_extender_2_out, multiplexer_1_out,
       multiplexer_2_out, or_1_out, shifter_1_out, shifter_2_out, shifter_3_out, subtractor_1_out, xor_1_out;

  ROM #(.addrWidth(3)) rom_1 (.addr(funct3), .data(rom_1_data));
  ROM #(.addrWidth(3)) rom_2 (.addr(funct3), .data(rom_1_data));
  assign and_1_out = rs1_out & rs2_out;  // AND_Gate and_1, 32 bits wide
  assign or_1_out = rs1_out | rs2_out;  // OR_Gate or_1, 32 bits wide
  Shifter #(.shift("ar"), .width(32)) shifter_1 (.in(rs1_out), .\dist (rs2_out[4:0]), .out(shifter_1_out));
  Shifter #(.shift("lr"), .width(32)) shifter_2 (.in(rs1_out), .\dist (rs2_out[4:0]), .out(shifter_2_out));
  assign xor_1_out = rs1_out ^ rs2_out;  // XOR_Gate xor_1, 32 bits wide
  Comparator #(.mode("unsigned"), .width(32)) comparator_1 (
    .a(rs1_out), .b(rs2_out), .lt(comparator_1_lt));  // open: gt, eq
  Comparator #(.width(32)) comparator_2 (.a(rs1_out), .b(rs2_out), .lt(comparator_2_lt));  // open: gt, eq
  Shifter #(.width(32)) shifter_3 (.in(rs1_out), .\dist (rs2_out[4:0]), .out(shifter_3_out));
  Subtractor #(.width(32)) subtractor_1 (.a(rs1_out), .b(rs2_out), .out(subtractor_1_out));  // open: bin, bout
  Adder #(.width(32)) adder_1 (.a(rs1_out), .b(rs2_out), .out(adder_1_out));  // open: cin, cout
  Comparator #(.width(7)) comparator_3 (.a(funct7), .b(7'b0100000), .eq(comparator_3_eq));  // open: gt, lt
  Multiplexer #(.width(32)) multiplexer_1 (
    .in0(shifter_1_out), .in1(shifter_2_out), .out(multiplexer_1_out), .sel(comparator_3_eq));
  assign bit_extender_1_out = {{31{1'b0}}, comparator_1_lt};  // Bit_Extender bit_extender_1
  assign bit_extender_2_out = {{31{1'b0}}, comparator_2_lt};  // Bit_Extender bit_extender_2
  Multiplexer #(.width(32)) multiplexer_2 (
    .in0(subtractor_1_out), .in1(adder_1_out), .out(multiplexer_2_out), .sel(comparator_3_eq));
  assign alu_out = rom_1_data[7] ? and_1_out : 32'bz;  // Controlled_Buffer controlled_buffer_1
  assign alu_out = rom_1_data[6] ? or_1_out : 32'bz;  // Controlled_Buffer controlled_buffer_2
  assign alu_out = rom_1_data[5] ? multiplexer_1_out : 32'bz;  // Controlled_Buffer controlled_buffer_3
  assign alu_out = rom_1_data[4] ? xor_1_out : 32'bz;  // Controlled_Buffer controlled_buffer_4
  assign alu_out = rom_1_data[3] ? bit_extender_1_out : 32'bz;  // Controlled_Buffer controlled_buffer_5
  assign alu_out = rom_1_data[2] ? bit_extender_2_out : 32'bz;  // Controlled_Buffer controlled_buffer_6
  assign alu_out = rom_1_data[1] ? shifter_3_out : 32'bz;  // Controlled_Buffer controlled_buffer_7
  assign alu_out = rom_1_data[0] ? multiplexer_2_out : 32'bz;  // Controlled_Buffer controlled_buffer_8

  // Notes on the sheet:
  //   contents of rom_1 (hex, n*v repeats v):
  //   1 2 4 8 10 20 40 80
  //   contents of rom_2 (hex, n*v repeats v):
  //   1 2 4 8 10 20 40 80
endmodule
